// Logisim project Lab3.circ as structural Verilog: 14 circuits, main circuit main
module main (
  input  RESET,
  input  [7:0] ENTRADA,
  input  INSERT,
  input  Pass_cl,
  input  Pass,
  input  HABI_a,
  input  [2:0] OP,
  input  Pass_ALU,
  input  HABI_b,
  input  HABI_c,
  input  in_11,
  input  in_12,
  input  in_13,
  output [7:0] SALIDA
);

  wire alu_1_out_5, alu_1_out_7, alu_1_sign, button_1_out, Contador_carry, not_1_out, not_2_out, not_3_out,
       not_4_out, not_5_out;
  wire [7:0] alu_1_s, Contador_q, Registro_a_q, Registro_b_q, Registro_c_q, Registro_d_q;

  not not_1 (not_1_out, Pass);
  _74245 #(.ShowInternalStructure("true")) u_74245_1 (
    .pin2(SALIDA[7]), .pin3(SALIDA[6]), .pin4(SALIDA[5]), .pin5(SALIDA[4]), .pin6(SALIDA[3]),
    .pin7(SALIDA[2]), .pin8(SALIDA[1]), .pin9(SALIDA[0]), .pin19(not_1_out), .pin18(ENTRADA[7]),
    .pin17(ENTRADA[6]), .pin16(ENTRADA[5]), .pin15(ENTRADA[4]), .pin14(ENTRADA[3]), .pin13(ENTRADA[2]),
    .pin12(ENTRADA[1]), .pin11(ENTRADA[0]));  // open: pin1
  Button button_1 (.out(button_1_out));
  Counter Contador (
    .clr(RESET), .load(INSERT), .clk(button_1_out), .D(SALIDA), .carry(Contador_carry), .Q(Contador_q));  // open: up, count
  Register Registro_a (.D(SALIDA), .en(HABI_a), .clk(button_1_out), .Q(Registro_a_q), .clr(RESET));
  Register Registro_b (.D(SALIDA), .en(HABI_b), .clk(button_1_out), .Q(Registro_b_q), .clr(RESET));
  Register Registro_c (.D(SALIDA), .en(HABI_c), .clk(button_1_out), .Q(Registro_c_q), .clr(RESET));
  Register Registro_d (.D(SALIDA), .en(in_12), .clk(button_1_out), .Q(Registro_d_q), .clr(RESET));
  LED led_1 (.in(Contador_carry));
  not not_2 (not_2_out, Pass_cl);
  _74245 #(.ShowInternalStructure("true")) u_74245_2 (
    .pin2(SALIDA[7]), .pin3(SALIDA[6]), .pin4(SALIDA[5]), .pin5(SALIDA[4]), .pin6(SALIDA[3]),
    .pin7(SALIDA[2]), .pin8(SALIDA[1]), .pin9(SALIDA[0]), .pin19(not_2_out), .pin18(Contador_q[7]),
    .pin17(Contador_q[6]), .pin16(Contador_q[5]), .pin15(Contador_q[4]), .pin14(Contador_q[3]),
    .pin13(Contador_q[2]), .pin12(Contador_q[1]), .pin11(Contador_q[0]));  // open: pin1
  not not_3 (not_3_out, in_11);
  _74245 #(.ShowInternalStructure("true")) u_74245_3 (
    .pin2(SALIDA[7]), .pin3(SALIDA[6]), .pin4(SALIDA[5]), .pin5(SALIDA[4]), .pin6(SALIDA[3]),
    .pin7(SALIDA[2]), .pin8(SALIDA[1]), .pin9(SALIDA[0]), .pin19(not_3_out), .pin18(Registro_c_q[7]),
    .pin17(Registro_c_q[6]), .pin16(Registro_c_q[5]), .pin15(Registro_c_q[4]), .pin14(Registro_c_q[3]),
    .pin13(Registro_c_q[2]), .pin12(Registro_c_q[1]), .pin11(Registro_c_q[0]));  // open: pin1
  not not_4 (not_4_out, in_13);
  _74245 #(.ShowInternalStructure("true")) u_74245_4 (
    .pin2(SALIDA[7]), .pin3(SALIDA[6]), .pin4(SALIDA[5]), .pin5(SALIDA[4]), .pin6(SALIDA[3]),
    .pin7(SALIDA[2]), .pin8(SALIDA[1]), .pin9(SALIDA[0]), .pin19(not_4_out), .pin18(Registro_d_q[7]),
    .pin17(Registro_d_q[6]), .pin16(Registro_d_q[5]), .pin15(Registro_d_q[4]), .pin14(Registro_d_q[3]),
    .pin13(Registro_d_q[2]), .pin12(Registro_d_q[1]), .pin11(Registro_d_q[0]));  // open: pin1
  ALU alu_1 (
    .A(Registro_a_q), .B(Registro_b_q), .OP(OP), .S(alu_1_s), .out_5(alu_1_out_5), .Sign(alu_1_sign),
    .out_7(alu_1_out_7));
  LED led_2 (.in(alu_1_out_5));
  LED led_3 (.in(alu_1_sign));
  LED led_4 (.in(alu_1_out_7));
  not not_5 (not_5_out, Pass_ALU);
  _74245 #(.ShowInternalStructure("true")) u_74245_5 (
    .pin2(SALIDA[7]), .pin3(SALIDA[6]), .pin4(SALIDA[5]), .pin5(SALIDA[4]), .pin6(SALIDA[3]),
    .pin7(SALIDA[2]), .pin8(SALIDA[1]), .pin9(SALIDA[0]), .pin19(not_5_out), .pin18(alu_1_s[7]),
    .pin17(alu_1_s[6]), .pin16(alu_1_s[5]), .pin15(alu_1_s[4]), .pin14(alu_1_s[3]), .pin13(alu_1_s[2]),
    .pin12(alu_1_s[1]), .pin11(alu_1_s[0]));  // open: pin1
endmodule

module SUM4 (
  input  [3:0] A,
  input  [3:0] B,
  input  Ce,
  output [3:0] S,
  output Cs
);

  _74283 #(.ShowInternalStructure("true")) u_74283_1 (
    .pin1(S[1]), .pin2(B[1]), .pin3(A[1]), .pin4(S[0]), .pin5(A[0]), .pin6(B[0]), .pin7(Ce), .pin15(B[2]),
    .pin14(A[2]), .pin13(S[2]), .pin12(A[3]), .pin11(B[3]), .pin10(S[3]), .pin9(Cs));
endmodule

module SUM8 (
  input  Ce,
  input  [7:0] A,
  input  [7:0] B,
  output [7:0] S,
  output Cs
);

  wire sum4_1_cs;

  SUM4 sum4_1 (.A(A[3:0]), .B(B[3:0]), .Ce(Ce), .S(S[3:0]), .Cs(sum4_1_cs));
  SUM4 sum4_2 (.A(A[7:4]), .B(B[7:4]), .Ce(sum4_1_cs), .S(S[7:4]), .Cs(Cs));
endmodule

module Complemento (
  input  [7:0] B,
  input  Op,
  output [7:0] S
);

  _7486 #(.ShowInternalStructure("true")) u_7486_1 (
    .pin1(B[7]), .pin2(Op), .pin3(S[7]), .pin4(B[6]), .pin5(Op), .pin6(S[6]), .pin13(B[5]), .pin12(Op),
    .pin11(S[5]), .pin10(B[4]), .pin9(Op), .pin8(S[4]));
  _7486 #(.ShowInternalStructure("true")) u_7486_2 (
    .pin1(B[3]), .pin2(Op), .pin3(S[3]), .pin4(B[2]), .pin5(Op), .pin6(S[2]), .pin13(B[1]), .pin12(Op),
    .pin11(S[1]), .pin10(B[0]), .pin9(Op), .pin8(S[0]));
endmodule

module sumador_8bit (
  input  [7:0] A,
  input  [7:0] B,
  input  S_R,
  output [7:0] S,
  output Co
);

  wire [7:0] complemento_1_s;

  SUM8 sum8_1 (.Ce(S_R), .A(A), .B(complemento_1_s), .S(S), .Cs(Co));
  Complemento complemento_1 (.B(B), .Op(S_R), .S(complemento_1_s));
endmodule

module MUX4_8bit (
  input  [7:0] AB,
  input  [7:0] AND_ent,
  input  [7:0] OR_ent,
  input  OP0,
  input  OP1,
  output [7:0] S
);

  wire [3:0] multiplexer_1_out, multiplexer_2_out;

  Multiplexer #(.enable("true"), .width(4)) multiplexer_1 (
    .in0(AND_ent[3:0]), .in1(OR_ent[3:0]), .out(multiplexer_1_out), .sel(OP0), .en(1'b1));
  Multiplexer #(.enable("true"), .width(4)) multiplexer_2 (
    .in0(AND_ent[7:4]), .in1(OR_ent[7:4]), .out(multiplexer_2_out), .sel(OP0), .en(1'b1));
  Multiplexer #(.enable("true"), .width(4)) multiplexer_3 (
    .in0(AB[3:0]), .in1(multiplexer_1_out), .out(S[3:0]), .sel(OP1), .en(1'b1));
  Multiplexer #(.enable("true"), .width(4)) multiplexer_4 (
    .in0(AB[7:4]), .in1(multiplexer_2_out), .out(S[7:4]), .sel(OP1), .en(1'b1));
endmodule

module Zero (
  input  [7:0] in_1,
  output Z
);

  wire or_1_out, or_2_out, or_3_out, or_4_out, or_5_out, or_6_out;

  or or_1 (or_1_out, in_1[0], in_1[1]);
  or or_2 (or_2_out, in_1[2], in_1[3]);
  or or_3 (or_3_out, in_1[4], in_1[5]);
  or or_4 (or_4_out, in_1[6], in_1[7]);
  or or_5 (or_5_out, or_1_out, or_2_out);
  or or_6 (or_6_out, or_3_out, or_4_out);
  nor nor_1 (Z, or_5_out, or_6_out);
endmodule

module Comp_and (
  input  [7:0] A,
  input  [7:0] B,
  output [7:0] S
);

  _7408 #(.ShowInternalStructure("true")) u_7408_1 (
    .pin1(A[7]), .pin2(B[7]), .pin3(S[7]), .pin4(B[6]), .pin5(A[6]), .pin6(S[6]), .pin13(A[5]), .pin12(B[5]),
    .pin11(S[5]), .pin10(A[4]), .pin9(B[4]), .pin8(S[4]));
  _7408 #(.ShowInternalStructure("true")) u_7408_2 (
    .pin1(A[1]), .pin2(B[1]), .pin3(S[1]), .pin4(A[0]), .pin5(B[0]), .pin6(S[0]), .pin13(B[3]), .pin12(A[3]),
    .pin11(S[3]), .pin10(A[2]), .pin9(B[2]), .pin8(S[2]));
endmodule

module comp_or (
  input  [7:0] A,
  input  [7:0] B,
  output [7:0] S
);

  _7432 #(.ShowInternalStructure("true")) u_7432_1 (
    .pin1(A[2]), .pin2(B[2]), .pin3(S[2]), .pin4(A[3]), .pin5(B[3]), .pin6(S[3]), .pin13(B[1]), .pin12(A[1]),
    .pin11(S[1]), .pin10(B[0]), .pin9(A[0]), .pin8(S[0]));
  _7432 #(.ShowInternalStructure("true")) u_7432_2 (
    .pin1(A[7]), .pin2(B[7]), .pin3(S[7]), .pin4(A[6]), .pin5(B[6]), .pin6(S[6]), .pin13(B[5]), .pin12(A[5]),
    .pin11(S[5]), .pin10(B[4]), .pin9(A[4]), .pin8(S[4]));
endmodule

module comp_xor (
  input  [7:0] A,
  input  [7:0] B,
  output [7:0] S
);

  _7486 #(.ShowInternalStructure("true")) u_7486_1 (
    .pin1(A[2]), .pin2(B[2]), .pin3(S[2]), .pin4(A[3]), .pin5(B[3]), .pin6(S[3]), .pin13(B[1]), .pin12(A[1]),
    .pin11(S[1]), .pin10(B[0]), .pin9(A[0]), .pin8(S[0]));
  _7486 #(.ShowInternalStructure("true")) u_7486_2 (
    .pin1(A[7]), .pin2(B[7]), .pin3(S[7]), .pin4(A[6]), .pin5(B[6]), .pin6(S[6]), .pin13(B[5]), .pin12(A[5]),
    .pin11(S[5]), .pin10(B[4]), .pin9(A[4]), .pin8(S[4]));
endmodule

module mux_7a1 (
  input  [7:0] AB,
  input  [7:0] INV,
  input  [7:0] DESPL_IZQ,
  input  [7:0] AND_op,
  input  [7:0] OR_op,
  input  [7:0] XOR_op,
  input  [2:0] OP_select,
  input  [7:0] DESPL_DER,
  output [7:0] S
);

  wire [7:0] mux4_8bit_1_s, mux4a1_1_s;

  MUX4_8bit mux4_8bit_1 (
    .AB(AB), .AND_ent(AND_op), .OR_ent(OR_op), .OP0(OP_select[0]), .OP1(OP_select[1]), .S(mux4_8bit_1_s));
  Mux4a1 mux4a1_1 (
    .XOR_ent(XOR_op), .DESPL_izq(DESPL_IZQ), .DESPL_der(DESPL_DER), .OP0(OP_select[0]), .OP1(OP_select[1]),
    .NEG(INV), .S(mux4a1_1_s));
  mux_2a1 mux_2a1_1 (.ent_uno(mux4_8bit_1_s), .ent_dos(mux4a1_1_s), .OP0(OP_select[2]), .S(S));
endmodule

module mux_2a1 (
  input  [7:0] ent_uno,
  input  [7:0] ent_dos,
  input  OP0,
  output [7:0] S
);

  _74157 u_74157_1 ();  // open: pin1, pin2, pin3, pin4, pin5, pin6, pin7, pin15, pin14, pin13, pin12, pin11, pin10, pin9
  Multiplexer #(.enable("true"), .width(4)) multiplexer_1 (
    .in0(ent_uno[3:0]), .in1(ent_dos[3:0]), .out(S[3:0]), .sel(OP0), .en(1'b1));
  Multiplexer #(.enable("true"), .width(4)) multiplexer_2 (
    .in0(ent_uno[7:4]), .in1(ent_dos[7:4]), .out(S[7:4]), .sel(OP0), .en(1'b1));
endmodule

module Mux4a1 (
  input  [7:0] XOR_ent,
  input  [7:0] DESPL_izq,
  input  [7:0] DESPL_der,
  input  OP0,
  input  OP1,
  input  [7:0] NEG,
  output [7:0] S
);

  wire [3:0] multiplexer_1_out, multiplexer_2_out, multiplexer_3_out, multiplexer_4_out;

  Multiplexer #(.enable("true"), .width(4)) multiplexer_1 (
    .in0(XOR_ent[3:0]), .in1(DESPL_izq[3:0]), .out(multiplexer_1_out), .sel(OP1), .en(1'b1));
  Multiplexer #(.enable("true"), .width(4)) multiplexer_2 (
    .in0(XOR_ent[7:4]), .in1(DESPL_izq[7:4]), .out(multiplexer_2_out), .sel(OP1), .en(1'b1));
  Multiplexer #(.enable("true"), .width(4)) multiplexer_3 (
    .in0(DESPL_der[3:0]), .in1(NEG[3:0]), .out(multiplexer_3_out), .sel(OP0), .en(1'b1));
  Multiplexer #(.enable("true"), .width(4)) multiplexer_4 (
    .in0(DESPL_der[7:4]), .in1(NEG[7:4]), .out(multiplexer_4_out), .sel(OP0), .en(1'b1));
  Multiplexer #(.enable("true"), .width(4)) multiplexer_5 (
    .in0(multiplexer_1_out), .in1(multiplexer_3_out), .out(S[3:0]), .sel(OP0), .en(1'b1));
  Multiplexer #(.enable("true"), .width(4)) multiplexer_6 (
    .in0(multiplexer_2_out), .in1(multiplexer_4_out), .out(S[7:4]), .sel(OP0), .en(1'b1));
endmodule

module ALU (
  input  [7:0] A,
  input  [7:0] B,
  input  [2:0] OP,
  output [7:0] S,
  output out_5,
  output Sign,
  output out_7
);

  wire [7:0] comp_and_1_s, comp_or_1_s, comp_xor_1_s, not_1_out, shifter_1_out, sumador_8bit_1_s;

  not not_1 (not_1_out[0], A[0]);
  not not_2 (not_1_out[1], A[1]);
  not not_3 (not_1_out[2], A[2]);
  not not_4 (not_1_out[3], A[3]);
  not not_5 (not_1_out[4], A[4]);
  not not_6 (not_1_out[5], A[5]);
  not not_7 (not_1_out[6], A[6]);
  not not_8 (not_1_out[7], A[7]);
  sumador_8bit sumador_8bit_1 (.A(A), .B(B), .S_R(OP[0]), .S(sumador_8bit_1_s), .Co(out_7));
  Comp_and comp_and_1 (.A(A), .B(B), .S(comp_and_1_s));
  comp_or comp_or_1 (.A(A), .B(B), .S(comp_or_1_s));
  comp_xor comp_xor_1 (.A(A), .B(B), .S(comp_xor_1_s));
  Shifter #(.shift("lr")) shifter_1 (.in(A), .\dist (3'b001), .out(shifter_1_out));
  mux_7a1 mux_7a1_1 (
    .AB(sumador_8bit_1_s), .INV(not_1_out), .DESPL_IZQ({A[6:0], A[7]}), .AND_op(comp_and_1_s),
    .OR_op(comp_or_1_s), .XOR_op(comp_xor_1_s), .OP_select(OP), .DESPL_DER(shifter_1_out), .S(S));
  Zero zero_1 (.in_1(S), .Z(out_5));

  assign Sign = S[7];
endmodule
