// Logisim project Proyecto2Circuito.circ as structural Verilog: 13 circuits, main circuit main
module main (
  input  [7:0] A,
  input  [7:0] B,
  input  [2:0] in_3,
  input  [2:0] nuevo,
  output [7:0] S,
  output out_6,
  output Sign,
  output out_8
);

  wire [7:0] comp_and_1_s, comp_or_1_s, comp_xor_1_s, not_1_out, shifter_1_out, sumador_8bit_1_s;

  not not_1 (not_1_out[0], A[0]);
  not not_2 (not_1_out[1], A[1]);
  not not_3 (not_1_out[2], A[2]);
  not not_4 (not_1_out[3], A[3]);
  not not_5 (not_1_out[4], A[4]);
  not not_6 (not_1_out[5], A[5]);
  not not_7 (not_1_out[6], A[6]);
  not not_8 (not_1_out[7], A[7]);
  sumador_8bit sumador_8bit_1 (.A(A), .B(B), .S_R(in_3[0]), .S(sumador_8bit_1_s), .Co(out_8));
  Comp_and comp_and_1 (.A(A), .B(B), .S(comp_and_1_s));
  comp_or comp_or_1 (.A(A), .B(B), .S(comp_or_1_s));
  comp_xor comp_xor_1 (.A(A), .B(B), .S(comp_xor_1_s));
  Shifter #(.shift("lr")) shifter_1 (.in(A), .\dist (nuevo), .out(shifter_1_out));
  mux_7a1 mux_7a1_1 (
    .AB(sumador_8bit_1_s), .INV(not_1_out), .DESPL_IZQ({A[6:0], A[7]}), .AND_op(comp_and_1_s),
    .OR_op(comp_or_1_s), .XOR_op(comp_xor_1_s), .OP_select(in_3), .DESPL_DER(shifter_1_out), .S(S));
  Zero zero_1 (.in_1(S), .Z(out_6));

  assign Sign = S[7];
endmodule

module SUM4 (
  input  [3:0] A,
  input  [3:0] B,
  input  Ce,
  output [3:0] S,
  output Cs
);

  _74283 #(.ShowInternalStructure("true")) u_74283_1 (
    .pin1(S[1]), .pin2(B[1]), .pin3(A[1]), .pin4(S[0]), .pin5(A[0]), .pin6(B[0]), .pin7(Ce), .pin15(B[2]),
    .pin14(A[2]), .pin13(S[2]), .pin12(A[3]), .pin11(B[3]), .pin10(S[3]), .pin9(Cs));
endmodule

module SUM8 (
  input  Ce,
  input  [7:0] A,
  input  [7:0] B,
  output [7:0] S,
  output Cs
);

  wire sum4_1_cs;

  SUM4 sum4_1 (.A(A[3:0]), .B(B[3:0]), .Ce(Ce), .S(S[3:0]), .Cs(sum4_1_cs));
  SUM4 sum4_2 (.A(A[7:4]), .B(B[7:4]), .Ce(sum4_1_cs), .S(S[7:4]), .Cs(Cs));
endmodule

module Complemento (
  input  [7:0] B,
  input  Op,
  output [7:0] S
);

  _7486 #(.ShowInternalStructure("true")) u_7486_1 (
    .pin1(B[7]), .pin2(Op), .pin3(S[7]), .pin4(B[6]), .pin5(Op), .pin6(S[6]), .pin13(B[5]), .pin12(Op),
    .pin11(S[5]), .pin10(B[4]), .pin9(Op), .pin8(S[4]));
  _7486 #(.ShowInternalStructure("true")) u_7486_2 (
    .pin1(B[3]), .pin2(Op), .pin3(S[3]), .pin4(B[2]), .pin5(Op), .pin6(S[2]), .pin13(B[1]), .pin12(Op),
    .pin11(S[1]), .pin10(B[0]), .pin9(Op), .pin8(S[0]));
endmodule

module sumador_8bit (
  input  [7:0] A,
  input  [7:0] B,
  input  S_R,
  output [7:0] S,
  output Co
);

  wire [7:0] complemento_1_s;

  SUM8 sum8_1 (.Ce(S_R), .A(A), .B(complemento_1_s), .S(S), .Cs(Co));
  Complemento complemento_1 (.B(B), .Op(S_R), .S(complemento_1_s));
endmodule

module MUX4_8bit (
  input  [7:0] AB,
  input  [7:0] AND_ent,
  input  [7:0] OR_ent,
  input  OP0,
  input  OP1,
  output [7:0] S
);

  wire [3:0] multiplexer_1_out, multiplexer_2_out;

  Multiplexer #(.enable("true"), .width(4)) multiplexer_1 (
    .in0(AND_ent[3:0]), .in1(OR_ent[3:0]), .out(multiplexer_1_out), .sel(OP0), .en(1'b1));
  Multiplexer #(.enable("true"), .width(4)) multiplexer_2 (
    .in0(AND_ent[7:4]), .in1(OR_ent[7:4]), .out(multiplexer_2_out), .sel(OP0), .en(1'b1));
  Multiplexer #(.enable("true"), .width(4)) multiplexer_3 (
    .in0(AB[3:0]), .in1(multiplexer_1_out), .out(S[3:0]), .sel(OP1), .en(1'b1));
  Multiplexer #(.enable("true"), .width(4)) multiplexer_4 (
    .in0(AB[7:4]), .in1(multiplexer_2_out), .out(S[7:4]), .sel(OP1), .en(1'b1));
endmodule

module Zero (
  input  [7:0] in_1,
  output Z
);

  wire or_1_out, or_2_out, or_3_out, or_4_out, or_5_out, or_6_out;

  or or_1 (or_1_out, in_1[0], in_1[1]);
  or or_2 (or_2_out, in_1[2], in_1[3]);
  or or_3 (or_3_out, in_1[4], in_1[5]);
  or or_4 (or_4_out, in_1[6], in_1[7]);
  or or_5 (or_5_out, or_1_out, or_2_out);
  or or_6 (or_6_out, or_3_out, or_4_out);
  nor nor_1 (Z, or_5_out, or_6_out);
endmodule

module Comp_and (
  input  [7:0] A,
  input  [7:0] B,
  output [7:0] S
);

  _7408 #(.ShowInternalStructure("true")) u_7408_1 (
    .pin1(A[7]), .pin2(B[7]), .pin3(S[7]), .pin4(B[6]), .pin5(A[6]), .pin6(S[6]), .pin13(A[5]), .pin12(B[5]),
    .pin11(S[5]), .pin10(A[4]), .pin9(B[4]), .pin8(S[4]));
  _7408 #(.ShowInternalStructure("true")) u_7408_2 (
    .pin1(A[1]), .pin2(B[1]), .pin3(S[1]), .pin4(A[0]), .pin5(B[0]), .pin6(S[0]), .pin13(B[3]), .pin12(A[3]),
    .pin11(S[3]), .pin10(A[2]), .pin9(B[2]), .pin8(S[2]));
endmodule

module comp_or (
  input  [7:0] A,
  input  [7:0] B,
  output [7:0] S
);

  _7432 #(.ShowInternalStructure("true")) u_7432_1 (
    .pin1(A[2]), .pin2(B[2]), .pin3(S[2]), .pin4(A[3]), .pin5(B[3]), .pin6(S[3]), .pin13(B[1]), .pin12(A[1]),
    .pin11(S[1]), .pin10(B[0]), .pin9(A[0]), .pin8(S[0]));
  _7432 #(.ShowInternalStructure("true")) u_7432_2 (
    .pin1(A[7]), .pin2(B[7]), .pin3(S[7]), .pin4(A[6]), .pin5(B[6]), .pin6(S[6]), .pin13(B[5]), .pin12(A[5]),
    .pin11(S[5]), .pin10(B[4]), .pin9(A[4]), .pin8(S[4]));
endmodule

module comp_xor (
  input  [7:0] A,
  input  [7:0] B,
  output [7:0] S
);

  _7486 #(.ShowInternalStructure("true")) u_7486_1 (
    .pin1(A[2]), .pin2(B[2]), .pin3(S[2]), .pin4(A[3]), .pin5(B[3]), .pin6(S[3]), .pin13(B[1]), .pin12(A[1]),
    .pin11(S[1]), .pin10(B[0]), .pin9(A[0]), .pin8(S[0]));
  _7486 #(.ShowInternalStructure("true")) u_7486_2 (
    .pin1(A[7]), .pin2(B[7]), .pin3(S[7]), .pin4(A[6]), .pin5(B[6]), .pin6(S[6]), .pin13(B[5]), .pin12(A[5]),
    .pin11(S[5]), .pin10(B[4]), .pin9(A[4]), .pin8(S[4]));
endmodule

module mux_7a1 (
  input  [7:0] AB,
  input  [7:0] INV,
  input  [7:0] DESPL_IZQ,
  input  [7:0] AND_op,
  input  [7:0] OR_op,
  input  [7:0] XOR_op,
  input  [2:0] OP_select,
  input  [7:0] DESPL_DER,
  output [7:0] S
);

  wire [7:0] mux4_8bit_1_s, mux4a1_1_s;

  MUX4_8bit mux4_8bit_1 (
    .AB(AB), .AND_ent(AND_op), .OR_ent(OR_op), .OP0(OP_select[0]), .OP1(OP_select[1]), .S(mux4_8bit_1_s));
  Mux4a1 mux4a1_1 (
    .XOR_ent(XOR_op), .DESPL_izq(DESPL_IZQ), .DESPL_der(DESPL_DER), .OP0(OP_select[0]), .OP1(OP_select[1]),
    .NEG(INV), .S(mux4a1_1_s));
  mux_2a1 mux_2a1_1 (.ent_uno(mux4_8bit_1_s), .ent_dos(mux4a1_1_s), .OP0(OP_select[2]), .S(S));
endmodule

module mux_2a1 (
  input  [7:0] ent_uno,
  input  [7:0] ent_dos,
  input  OP0,
  output [7:0] S
);

  _74157 u_74157_1 ();  // open: pin1, pin2, pin3, pin4, pin5, pin6, pin7, pin15, pin14, pin13, pin12, pin11, pin10, pin9
  Multiplexer #(.enable("true"), .width(4)) multiplexer_1 (
    .in0(ent_uno[3:0]), .in1(ent_dos[3:0]), .out(S[3:0]), .sel(OP0), .en(1'b1));
  Multiplexer #(.enable("true"), .width(4)) multiplexer_2 (
    .in0(ent_uno[7:4]), .in1(ent_dos[7:4]), .out(S[7:4]), .sel(OP0), .en(1'b1));
endmodule

module Mux4a1 (
  input  [7:0] XOR_ent,
  input  [7:0] DESPL_izq,
  input  [7:0] DESPL_der,
  input  OP0,
  input  OP1,
  input  [7:0] NEG,
  output [7:0] S
);

  wire [3:0] multiplexer_1_out, multiplexer_2_out, multiplexer_3_out, multiplexer_4_out;

  Multiplexer #(.enable("true"), .width(4)) multiplexer_1 (
    .in0(XOR_ent[3:0]), .in1(DESPL_izq[3:0]), .out(multiplexer_1_out), .sel(OP1), .en(1'b1));
  Multiplexer #(.enable("true"), .width(4)) multiplexer_2 (
    .in0(XOR_ent[7:4]), .in1(DESPL_izq[7:4]), .out(multiplexer_2_out), .sel(OP1), .en(1'b1));
  Multiplexer #(.enable("true"), .width(4)) multiplexer_3 (
    .in0(DESPL_der[3:0]), .in1(NEG[3:0]), .out(multiplexer_3_out), .sel(OP0), .en(1'b1));
  Multiplexer #(.enable("true"), .width(4)) multiplexer_4 (
    .in0(DESPL_der[7:4]), .in1(NEG[7:4]), .out(multiplexer_4_out), .sel(OP0), .en(1'b1));
  Multiplexer #(.enable("true"), .width(4)) multiplexer_5 (
    .in0(multiplexer_1_out), .in1(multiplexer_3_out), .out(S[3:0]), .sel(OP0), .en(1'b1));
  Multiplexer #(.enable("true"), .width(4)) multiplexer_6 (
    .in0(multiplexer_2_out), .in1(multiplexer_4_out), .out(S[7:4]), .sel(OP0), .en(1'b1));
endmodule
